# Fritzing sketch circuitry (saved by Fritzing 1.0.6)

parts:
  Part1 = Adafruit Metro ESP32-S3 [part_number="Adafruit #5500"]
  Part2 = Motor Driver 1A Dual TB6612FNG
  DC_Mot_Enc1 = DC Motor with two-phase hall-encoder [part_number=VT-E-G25A-06-177E]
  DC_Mot_Enc2 = DC Motor with two-phase hall-encoder [part_number=VT-E-G25A-06-177E]
  MPU-1 = Adafruit MPU6050
  U1 = LIPO-110mAh [package=lipo-110]
  U2 = LIPO-2000mAh [package=lipo-2000]
  A1 = Seeed mlx90640 thermal imaging camera
  M1 = RPlidar A1M8 [package=THT]
  A2 = WMYCONGCONG buck converter

nets:
  N1: Part1.SCL, MPU-1.SCL, A1.Pin_1, A1.Pin_8
  N2: Part1.SDA, MPU-1.SDA, A1.Pin_2, A1.Pin_7
  VCC: Part1.3.3V, Part2.VCC, DC_Mot_Enc1.pin3, DC_Mot_Enc2.pin3, MPU-1.VCC, A1.Pin_3, A1.Pin_6
  GND: Part1.GND, Part2.GND, DC_Mot_Enc1.pin5, DC_Mot_Enc2.pin5, MPU-1.GND, U1.-, U2.-, A1.Pin_4, A1.Pin_5, A2.Pin_3
  N3: Part1.D12, DC_Mot_Enc1.pin6
  N4: Part1.D11, DC_Mot_Enc1.pin4
  N5: Part1.D10, DC_Mot_Enc2.pin6
  N6: Part1.D9, DC_Mot_Enc2.pin4
  N7: Part1.D8, Part2.PWMB
  N8: Part1.D7, Part2.BIN2
  N9: Part1.D6, Part2.BIN1
  N10: Part1.D5, Part2.STBY
  N11: Part1.D4, Part2.AIN1
  N12: Part1.D3, Part2.AIN2
  N13: Part1.D2, Part2.PWMA
  N14: Part1.TDI_RX, M1.pin1
  N15: Part1.VBAT, U1.+
  N16: Part2.B01, DC_Mot_Enc1.pin2
  N17: Part2.B02, DC_Mot_Enc1.pin1
  N18: Part2.A01, DC_Mot_Enc2.pin1
  N19: Part2.VM, U2.+, A2.Pin_2
  N20: M1.pin3, A2.Pin_1
  N21: M1.pin4, A2.Pin_4

notes:
  LiDAR
  IMU
  Thermal Sensor
  Motor Driver
  Voltage Converter
  Motor (x2)
  ESP32-S3 Metro
  Motor Battery
  Board Battery

custom parts:
  Adafruit Metro ESP32-S3: What's Metro-shaped and has an ESP32-S3 WiFi module? What has a STEMMA QT connector for I2C devices and a Lipoly charger circuit? What has your favorite Espressif WiFi microcontroller and lots of memory for your next IoT project? That's right - it's the new Adafruit Metro ESP32-S3! With native USB and a load of PSRAM, this board is perfect for use with CircuitPython or Arduino to add low-cost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
  Adafruit MPU6050: The MPU-6050 is a popular six axis accelerometer and gyroscope (gyro) that has all the info you need on how things are shakin' and spinnin' . With six axes of sensing and 16-bit measurements, you'll have everything you need to give your robot friend an inner ear. This combination of gyroscopes and accelerometers is commonly referred to as an Inertial Measurement Unit or IMU. Not so long ago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
  Seeed mlx90640 thermal imaging camera: Grove - Thermal Imaging Camera is a thermal sensor which carries MLX90640 IR Array. The camera can present dynamic thermal images and detect the surrounding temperature from -40℃~300℃.
  RPlidar A1M8: .The RPLIDAR A1 is the next generation low cost 360 degree 2D laser scanner (LIDAR) solution developed by SLAMTEC. It can take up to 4000 samples of laser ranging per second with high rotation speed. And equipped with SLAMTEC patented OPTMAG technology, it breakouts the life limitation of traditional LIDAR system so as to work stably for a long time.
  WMYCONGCONG buck converter: These amazing little DC-DC converters feature a wide input voltage of 4.5-24V and the output voltage can be set to one of six fixed voltages, or fully variable, just by bridging the relevant solder pads on the back of the PCB..
